// Logisim project ExpSplitters..circ as structural Verilog
module Ex4 (
  input  [7:0] In,
  output [7:0] out_2,
  output Out1,
  output [7:0] Out2
);

  assign Out2 = ~In;  // NOT_Gate not_1, 8 bits wide
  and and_1 (Out1, In[0], In[7]);

  assign out_2 = In;
endmodule

module Ex5 (
  input  [15:0] A,
  input  [3:0] B,
  output [15:0] out_3
);

  wire [1:0] multiplexer_1_out_2;
  wire [3:0] multiplexer_2_out_2;
  wire [7:0] multiplexer_3_out, multiplexer_3_out_2;
  wire [11:0] multiplexer_2_out;
  wire [13:0] multiplexer_1_out;

  Multiplexer #(.width(16)) multiplexer_1 (
    .in0(A), .in1({A[0], A[15:1]}), .out({multiplexer_1_out, multiplexer_1_out_2}), .sel(B[0]));  // open: en
  Multiplexer #(.width(16)) multiplexer_2 (
    .in0({multiplexer_1_out, multiplexer_1_out_2}), .in1({multiplexer_1_out_2, multiplexer_1_out}),
    .out({multiplexer_2_out, multiplexer_2_out_2}), .sel(B[1]));  // open: en
  Multiplexer #(.width(16)) multiplexer_3 (
    .in0({multiplexer_2_out, multiplexer_2_out_2}), .in1({multiplexer_2_out_2, multiplexer_2_out}),
    .out({multiplexer_3_out, multiplexer_3_out_2}), .sel(B[2]));  // open: en
  Multiplexer #(.width(16)) multiplexer_4 (
    .in0({multiplexer_3_out, multiplexer_3_out_2}), .in1({multiplexer_3_out_2, multiplexer_3_out}),
    .out(out_3), .sel(B[3]));  // open: en
endmodule
