// Logisim project makingGates.circ as structural Verilog: 7 circuits, main circuit main
module main (
  input  in_1,
  input  in_2,
  input  in_3,
  input  in_4,
  output out_5,
  output out_6,
  output [7:0] out_7,
  output [7:0] out_8
);

  AddMachine addmachine_1 (.out_1(out_7), .out_2(out_8));
  NAND nand_1 (.lb1(in_1), .lb2(in_2), .out_3(out_5));
  XOR xor_1 (.lb1(in_3), .lb2(in_4), .out_3(out_6));
endmodule

module NAND (
  input  lb1,
  input  lb2,
  output out_3
);

  wire and_1_out;

  not not_1 (out_3, and_1_out);
  and and_1 (and_1_out, lb1, lb1, lb2);
endmodule

module XOR (
  input  lb1,
  input  lb2,
  output out_3
);

  wire and_1_out, and_2_out, not_1_out, not_2_out;

  not not_1 (not_1_out, lb1);
  not not_2 (not_2_out, lb2);
  and and_1 (and_1_out, lb2, not_1_out);
  and and_2 (and_2_out, lb1, not_2_out);
  or or_1 (out_3, and_1_out, and_2_out);
endmodule

module _2_to_1_MUX (
  input  A,
  input  X,
  input  B
);

  wire and_1_out, and_2_out, not_1_out;

  not not_1 (not_1_out, X);
  and and_1 (and_1_out, A, not_1_out);
  and and_2 (and_2_out, X, B);
  // OR_Gate or_1 has open pins: in1=and_1_out, in3=and_2_out, out=open
endmodule

module _4_to_1_MUX (
  input  X,
  input  Y,
  input  in_3,
  input  A,
  input  B,
  input  C,
  input  D,
  output out_8
);

  wire and_1_out, and_2_out, and_3_out, and_4_out, not_2_out;

  not not_1 (B, X);
  not not_2 (not_2_out, Y);
  and and_1 (and_1_out, not_2_out, B, A);
  and and_2 (and_2_out, Y, B, B);
  and and_3 (and_3_out, not_2_out, X, C);
  and and_4 (and_4_out, Y, X, D);
  or or_1 (out_8, and_1_out, and_2_out, and_3_out, and_4_out);
endmodule

module NOR (
  input  in_1,
  input  in_2,
  output out_3
);

  wire or_1_out;

  or or_1 (or_1_out, in_1, in_2);
  not not_1 (out_3, or_1_out);
endmodule

module AddMachine (
  output [7:0] out_1,
  output [7:0] out_2
);

  wire clock_1_out;

  Adder adder_1 (.a(8'h1), .b(out_2), .out(out_1));  // open: cin, cout
  Clock clock_1 (.out(clock_1_out));
  Register register_1 (.D(out_1), .Q(out_2), .clk(clock_1_out));  // open: en, clr
endmodule
